# Fritzing sketch Motor Assignment [Unzi Brian] (saved by Fritzing 0.8.7b)
breadboards: 1

parts:
  S1 = Pushbutton [package="[SMD]"]
  R1 = Resistor [tolerance=±5% resistance=220 package=THT]
  Part1 = Arduino Uno (Rev3) - ICSP
  J1 = Basic Servo

nets:
  N1: S1.Pin_1, S1.Pin_2
  5V: S1.Pin_3, S1.Pin_4, R1.Pin_1, Part1.D13/SCK, Part1.5V, J1.vcc
  N2: Part1.D9_PWM, J1.pulse
  GND: Part1.GND, J1.gnd
